# Fritzing sketch Spark.Core.MPL115A2 (saved by Fritzing 0.9.1b)
circuit board: 8.46667cm x 5.64444cm
breadboards: 1

parts:
  Spark_io_Core = Spark Core (v1.0)
  DHT22 = Humidity and Temperature Sensor RHT03
  R1 = Resistor [tolerance=±5% resistance=10k package="0805 [SMD]"]
  MPL115A2 = MPL3115A2 [package=lga8]

nets (from the schematic view):
  N1: Spark_io_Core.A0, DHT22.Data-signal, R1.Pin_1
  GND: Spark_io_Core.GND, DHT22.GND_2, MPL115A2.GND
  N2: Spark_io_Core.D0, MPL115A2.SDA
  N3: Spark_io_Core.D1, MPL115A2.SCL
  3V3: Spark_io_Core.3V3, DHT22.Vcc, R1.Pin_0, MPL115A2.VDD
